# Fritzing sketch Devre Şeması (saved by Fritzing 0.9.2b)

parts:
  U1 = ESP8266 NodeMCU LoLin base
  LED1 = RGB LED (com. anode, rbg) [package="5 mm [THT]"]

nets:
  N1: U1.3V1-0, U1.3V3-0, LED1.red_cathode
  N2: U1.D5-2, U1.D5-3, LED1.common_anode
  N3: U1.D6-2, LED1.blue_cathode
  N4: U1.D7-1, U1.D7-2, LED1.green_cathode

custom parts:
  ESP8266 NodeMCU LoLin base: ESP8266 based NodeMCU Base
